# Fritzing sketch rover_one-2 (saved by Fritzing 0.9.3b)
circuit board: 10cm x 10cm
breadboards: 1

parts:
  IC3 = L9110H [chip_label=IC package="DIP (Dual Inline) [THT]"]
  LED4 = LED - 5mm [color="Red (633nm)" package="5 mm [THT]"]
  LED3 = LED - 5mm [color="Red (633nm)" package="5 mm [THT]"]
  LED5 = LED - 5mm [color="White (6500K)" package="5 mm [THT]"]
  LED2 = LED - 5mm [color="Blue (430nm)" package="5 mm [THT]"]
  LED1 = LED - 5mm [color="Blue (430nm)" package="5 mm [THT]"]
  LED6 = LED - 5mm [color="White (6500K)" package="5 mm [THT]"]
  IC1 = 74HC595 [package="DIP16 [THT]"]
  M1 = DC Motor
  LED7 = LED - 5mm [color="Yellow (592nm)" package="5 mm [THT]"]
  LED8 = LED - 5mm [color="Yellow (592nm)" package="5 mm [THT]"]
  HCSR-1 = hc-sr04
  HCSR-3 = hc-sr04
  HCSR-4 = hc-sr04
  VCC1 = Battery block 9V
  IC2 = 74HC595 [package="DIP16 [THT]"]
  LED9 = LED - 5mm [color="Yellow (592nm)" package="5 mm [THT]"]
  LED10 = LED - 5mm [color="Yellow (592nm)" package="5 mm [THT]"]
  LED14 = LED - 5mm [color="Infrared (940nm)" package="5 mm [THT]"]
  LED13 = LED - 5mm [color="Infrared (940nm)" package="5 mm [THT]"]
  LED12 = LED - 5mm [color="Infrared (940nm)" package="5 mm [THT]"]
  LED11 = LED - 5mm [color="Infrared (940nm)" package="5 mm [THT]"]
  LED16 = LED - 5mm [color="Infrared (940nm)" package="5 mm [THT]"]
  LED15 = LED - 5mm [color="Infrared (940nm)" package="5 mm [THT]"]
  Servo1 = Basic Servo
  C1 = Electrolytic Capacitor [capacitance=470µF voltage=35V package="200 mil [THT, electrolytic]"]  # not connected
  LDR1 = Photocell (LDR) [package=THT]
  DS1 = DS18B20 1-Wire Temperature Sensor [part_number=DS18B20]
  Arduino_Nano = Arduino Nano (Rev3.0)
  R15 = Resistor [tolerance=±5% resistance=220 package=THT]
  R16 = Resistor [tolerance=±5% resistance=220 package=THT]
  R14 = Resistor [tolerance=±5% resistance=220 package=THT]
  R13 = Resistor [tolerance=±5% resistance=220 package=THT]
  R12 = Resistor [tolerance=±5% resistance=220 package=THT]
  R11 = Resistor [tolerance=±5% resistance=220 package=THT]
  R10 = Resistor [tolerance=±5% resistance=220 package=THT]
  R9 = Resistor [tolerance=±5% resistance=220 package=THT]
  R18 = Resistor [tolerance=±5% resistance=4.7k package=THT]
  R1 = Resistor [tolerance=±5% resistance=220 package=THT]
  R2 = Resistor [tolerance=±5% resistance=220 package=THT]
  R3 = Resistor [tolerance=±5% resistance=220 package=THT]
  R4 = Resistor [tolerance=±5% resistance=220 package=THT]
  R5 = Resistor [tolerance=±5% resistance=220 package=THT]
  R6 = Resistor [tolerance=±5% resistance=220 package=THT]
  R7 = Resistor [tolerance=±5% resistance=220 package=THT]
  R8 = Resistor [tolerance=±5% resistance=220 package=THT]
  R17 = Resistor [tolerance=±5% resistance=100k package=THT]
  HCSR-2 = hc-sr04

nets:
  N1: IC3.OA, M1.pin_2
  N2: IC3.VCC, VCC1.+
  N3: IC3.OB, M1.pin_1
  GND: IC3.GND, LED4.anode, LED3.anode, LED5.anode, LED2.anode, LED1.anode, LED6.anode, IC1.GND, IC1.OE, LED7.anode, LED8.anode, HCSR-1.GND, HCSR-3.GND, HCSR-4.GND, VCC1.-, IC2.GND, IC2.OE, LED9.anode, LED10.anode, LED14.anode, LED13.anode, LED12.anode, LED11.anode, LED16.anode, LED15.anode, DS1.GND, Arduino_Nano.GND, R17.Pin_1, HCSR-2.GND
  N4: IC3.IA, Arduino_Nano.D5
  N5: IC3.IB, Arduino_Nano.D4
  N6: LED4.cathode, R4.Pin_1
  N7: LED3.cathode, R3.Pin_1
  N8: LED5.cathode, R5.Pin_1
  N9: LED2.cathode, R2.Pin_1
  N10: LED1.cathode, R1.Pin_1
  N11: LED6.cathode, R6.Pin_1
  N12: IC1.Q1, R2.Pin_0
  N13: IC1.Q2, R3.Pin_0
  N14: IC1.Q3, R4.Pin_0
  N15: IC1.Q4, R5.Pin_0
  N16: IC1.Q5, R6.Pin_0
  N17: IC1.Q6, R7.Pin_0
  N18: IC1.Q7, R8.Pin_0
  N19: IC1.Q7', IC2.DS
  VCC: IC1.MR, IC1.VCC, HCSR-1.VCC, HCSR-3.VCC, HCSR-4.VCC, IC2.MR, IC2.VCC, LDR1.pin_1, DS1.VDD, Arduino_Nano.5V, R18.Pin_1, HCSR-2.VCC
  N20: IC1.SH_CP, IC2.SH_CP, Arduino_Nano.D13/SCK
  N21: IC1.ST_CP, IC2.ST_CP, Arduino_Nano.D12/MISO
  N22: IC1.DS, Arduino_Nano.D11/MOSI
  N23: IC1.Q0, R1.Pin_0
  N24: LED7.cathode, R7.Pin_1
  N25: LED8.cathode, R8.Pin_1
  N26: HCSR-1.Trig, HCSR-1.Echo, Arduino_Nano.D10
  N27: HCSR-3.Trig, HCSR-3.Echo, Arduino_Nano.D8
  N28: HCSR-4.Trig, HCSR-4.Echo, Arduino_Nano.D7
  N29: IC2.Q1, R10.Pin_0
  N30: IC2.Q2, R11.Pin_0
  N31: IC2.Q3, R12.Pin_0
  N32: IC2.Q4, R13.Pin_0
  N33: IC2.Q5, R14.Pin_0
  N34: IC2.Q6, R15.Pin_0
  N35: IC2.Q7, R16.Pin_0
  N36: IC2.Q0, R9.Pin_0
  N37: LED9.cathode, R9.Pin_1
  N38: LED10.cathode, R10.Pin_1
  N39: LED14.cathode, R14.Pin_1
  N40: LED13.cathode, R13.Pin_1
  N41: LED12.cathode, R12.Pin_1
  N42: LED11.cathode, R11.Pin_1
  N43: LED16.cathode, R16.Pin_1
  N44: LED15.cathode, R15.Pin_1
  N45: Servo1.pulse, Arduino_Nano.D6
  N46: LDR1.pin_0, Arduino_Nano.A0, R17.Pin_0
  N47: DS1.DQ, Arduino_Nano.D2, R18.Pin_0
  N48: Arduino_Nano.D9, HCSR-2.Trig, HCSR-2.Echo

custom parts:
  L9110H: The ASIC device control and drive motor design two-channel push-pull power amplifier discrete circuits integrated into a monolithic IC, peripheral devices and reduce the cost, improve the reliability of the whole. This chip has two TTL / CMOS compatible with the level of the input, with good resistance; two output terminals can directly forward and reverse movement of the drive motor, it has a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
