# Fritzing sketch rover_one (saved by Fritzing 0.9.3b)
circuit board: 10cm x 6cm
breadboards: 1

parts:
  IC1 = L9110H [chip_label=IC package="DIP (Dual Inline) [THT]"]
  LED1 = LED - 5mm [color="Red (633nm)" package="5 mm [THT]"]
  LED2 = LED - 5mm [color="Red (633nm)" package="5 mm [THT]"]
  LED3 = LED - 5mm [color="White (6500K)" package="5 mm [THT]"]
  LED5 = LED - 5mm [color="Blue (430nm)" package="5 mm [THT]"]
  LED6 = LED - 5mm [color="Blue (430nm)" package="5 mm [THT]"]
  LED7 = LED - 5mm [color="White (6500K)" package="5 mm [THT]"]
  R1 = Resistor [tolerance=±5% resistance=220 package="2512 [SMD]"]
  U1 = 74HC595 [package="DIP16 [THT]"]
  R2 = Resistor [tolerance=±5% resistance=220 package="2512 [SMD]"]
  R3 = Resistor [tolerance=±5% resistance=220 package="2512 [SMD]"]
  R4 = Resistor [tolerance=±5% resistance=220 package="2512 [SMD]"]
  R6 = Resistor [tolerance=±5% resistance=220 package="2512 [SMD]"]
  M1 = DC Motor
  LED8 = LED - 5mm [color="Yellow (592nm)" package="5 mm [THT]"]
  LED9 = LED - 5mm [color="Yellow (592nm)" package="5 mm [THT]"]
  R7 = Resistor [tolerance=±5% resistance=220 package="2512 [SMD]"]
  R8 = Resistor [tolerance=±5% resistance=220 package="2512 [SMD]"]
  Part2 = Arduino Uno (Rev3)
  hc-sr2 = hc-sr04
  hc-sr3 = hc-sr04
  hc-sr4 = hc-sr04
  hc-sr5 = hc-sr04
  VCC1 = Battery block 9V
  U2 = 74HC595 [package="DIP16 [THT]"]
  LED10 = LED - 5mm [color="Yellow (592nm)" package="5 mm [THT]"]
  LED11 = LED - 5mm [color="Yellow (592nm)" package="5 mm [THT]"]
  LED12 = LED - 5mm [color="Infrared (940nm)" package="5 mm [THT]"]
  LED13 = LED - 5mm [color="Infrared (940nm)" package="5 mm [THT]"]
  LED14 = LED - 5mm [color="Infrared (940nm)" package="5 mm [THT]"]
  LED15 = LED - 5mm [color="Infrared (940nm)" package="5 mm [THT]"]
  LED16 = LED - 5mm [color="Infrared (940nm)" package="5 mm [THT]"]
  LED17 = LED - 5mm [color="Infrared (940nm)" package="5 mm [THT]"]
  R9 = Resistor [tolerance=±5% resistance=220 package="2512 [SMD]"]
  R10 = Resistor [tolerance=±5% resistance=220 package="2512 [SMD]"]
  R11 = Resistor [tolerance=±5% resistance=220 package="2512 [SMD]"]
  R12 = Resistor [tolerance=±5% resistance=220 package="2512 [SMD]"]
  R13 = Resistor [tolerance=±5% resistance=220 package="2512 [SMD]"]
  R14 = Resistor [tolerance=±5% resistance=220 package="2512 [SMD]"]
  R15 = Resistor [tolerance=±5% resistance=220 package="2512 [SMD]"]
  R16 = Resistor [tolerance=±5% resistance=220 package="2512 [SMD]"]
  J1 = Basic Servo
  C3 = Electrolytic Capacitor [capacitance=470µF voltage=35V package="200 mil [THT, electrolytic]"]
  R5 = Resistor [tolerance=±5% resistance=220 package="2512 [SMD]"]
  R19 = Photocell (LDR) [package=THT]
  R20 = Resistor [tolerance=±5% resistance=100k package="2512 [SMD]"]
  R21 = Resistor [tolerance=±5% resistance=4.7k package="2512 [SMD]"]
  DS1 = DS18B20 1-Wire Temperature Sensor [part_number=DS18B20]

nets:
  N1: IC1.OA, M1.pin_2
  N2: IC1.VCC, VCC1.+
  N3: IC1.OB, M1.pin_1
  GND: IC1.GND, U1.GND, U1.OE, Part2.GND, hc-sr2.GND, hc-sr3.GND, hc-sr4.GND, hc-sr5.GND, VCC1.-, U2.GND, U2.OE, LED10.anode, LED11.anode, LED12.anode, LED13.anode, LED14.anode, LED15.anode, LED16.anode, LED17.anode, J1.gnd, C3.-, R20.Pin_1, DS1.GND
  N4: IC1.IA, Part2.D5_PWM
  N5: IC1.IB, Part2.D4
  N6: LED1.cathode, R2.Pin_1
  N7: LED1.anode, LED2.anode, LED3.anode, LED5.anode, LED6.anode, LED7.anode, LED8.anode, LED9.anode
  N8: LED2.cathode, R4.Pin_1
  N9: LED3.cathode, R3.Pin_1
  N10: LED5.cathode, R5.Pin_1
  N11: LED6.cathode, R6.Pin_1
  N12: LED7.cathode, R1.Pin_1
  N13: R1.Pin_0, U1.Q5
  N14: U1.Q1, R5.Pin_0
  N15: U1.Q2, R4.Pin_0
  N16: U1.Q3, R2.Pin_0
  N17: U1.Q4, R3.Pin_0
  N18: U1.Q6, R7.Pin_0
  N19: U1.Q7, R8.Pin_0
  N20: U1.Q7', U2.DS
  VCC: U1.MR, U1.VCC, Part2.5V, hc-sr2.VCC, hc-sr3.VCC, hc-sr4.VCC, hc-sr5.VCC, U2.MR, U2.VCC, J1.vcc, C3.+, R19.pin_1, R21.Pin_1, DS1.VDD
  N21: U1.SH_CP, Part2.D13/SCK, U2.SH_CP
  N22: U1.ST_CP, Part2.D12/MISO, U2.ST_CP
  N23: U1.DS, Part2.D11_PWM/MOSI
  N24: U1.Q0, R6.Pin_0
  N25: LED8.cathode, R7.Pin_1
  N26: LED9.cathode, R8.Pin_1
  N27: Part2.A0, R19.pin_0, R20.Pin_0
  N28: Part2.D8, hc-sr4.Trig, hc-sr4.Echo
  N29: Part2.D9_PWM, hc-sr3.Trig, hc-sr3.Echo
  N30: Part2.D10_PWM/SS, hc-sr2.Trig, hc-sr2.Echo
  N31: Part2.D2, R21.Pin_0, DS1.DQ
  N32: Part2.D6_PWM, J1.pulse
  N33: Part2.D7, hc-sr5.Trig, hc-sr5.Echo
  N34: U2.Q1, R15.Pin_0
  N35: U2.Q2, R14.Pin_0
  N36: U2.Q3, R13.Pin_0
  N37: U2.Q4, R12.Pin_0
  N38: U2.Q5, R11.Pin_0
  N39: U2.Q6, R10.Pin_0
  N40: U2.Q7, R9.Pin_0
  N41: U2.Q0, R16.Pin_0
  N42: LED10.cathode, R16.Pin_1
  N43: LED11.cathode, R15.Pin_1
  N44: LED12.cathode, R11.Pin_1
  N45: LED13.cathode, R12.Pin_1
  N46: LED14.cathode, R13.Pin_1
  N47: LED15.cathode, R14.Pin_1
  N48: LED16.cathode, R9.Pin_1
  N49: LED17.cathode, R10.Pin_1

custom parts:
  L9110H: The ASIC device control and drive motor design two-channel push-pull power amplifier discrete circuits integrated into a monolithic IC, peripheral devices and reduce the cost, improve the reliability of the whole. This chip has two TTL / CMOS compatible with the level of the input, with good resistance; two output terminals can directly forward and reverse movement of the drive motor, it has a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
